# Fritzing sketch circutDesign (saved by Fritzing 0.9.3b)

parts:
  Raspberry_Pi_Zero1 = Raspberry Pi Zero
  U1 = WS2812 RGB LED strip
  J1 = screw terminal, 4 pins
  J2 = Screw terminal - 2 pins [package=THT]

nets:
  N1: Raspberry_Pi_Zero1.GND, J2.pin2
  N2: Raspberry_Pi_Zero1.GPIO18, U1.DIN, J2.pin1
  N3: U1.GND, J1.pin2
  N4: U1.VCC, J1.pin3

custom parts:
  WS2812 RGB LED strip: WS2812 strip
